# Fritzing sketch dht with servo (saved by Fritzing 0.9.2b)
breadboards: 1

parts:
  Part1 = Arduino Uno (Rev3)
  DHT-11 = DHT11 Humitidy and Temperature Sensor
  J1 = Basic Servo
  R1 = Resistor [tolerance=±5% resistance=10k package=THT]
  C1_100uF = Capacitor Polarized [package=cpol-radial-100uf-25v]

nets:
  GND: Part1.GND, DHT-11.GND, J1.gnd, C1_100uF.+
  N1: Part1.D2, DHT-11.DATA, R1.Pin_1
  N2: Part1.D3_PWM, J1.pulse
  N3: Part1.RESET, C1_100uF.-
  5V: Part1.5V, DHT-11.VDD, J1.vcc, R1.Pin_0

custom parts:
  DHT11 Humitidy and Temperature Sensor: DHT11 Humidity and Temperature Sensor
