# Fritzing sketch hall sensor (saved by Fritzing 0.9.2b)

parts:
  Part1 = Arduino Uno (Rev3)
  R1 = Resistor [tolerance=±5% resistance=10k package=THT]
  Hall_Sensor = mystery part, 3 pins [chip_label=?]

nets:
  N1: Part1.D12/MISO, R1.Pin_1, Hall_Sensor.pin3
  N2: Part1.GND, Hall_Sensor.pin2
  N3: Part1.5V, R1.Pin_0, Hall_Sensor.pin1
